# Fritzing sketch led1 (saved by Fritzing 0.9.4)
breadboards: 1

parts:
  R1 = Resistor [tolerance=±5% resistance=220 package=THT]
  LED1 = LED - 5mm [color="Red (633nm)" package="5 mm [THT]"]
  Part2 = Arduino Prototyping Shield

nets:
  N1: R1.Pin_0, Part2.D13
  N2: R1.Pin_1, LED1.anode
  N3: LED1.cathode, Part2.GND

// code stored in the sketch: led1.ino
int led = 13
void setup(){
    pinMode(led,OUTPUT);
}
void loop(){
    digitalWrite(led,HIGH);
    delay(1000);
    digitalWrite(led,LOW);
    delay(1000);
}
